// Logisim project Warmup.circ as structural Verilog: 2 circuits, main circuit main
module main (
  input  A,
  input  B,
  output f
);

  wire not_1_out;

  not not_1 (not_1_out, B);
  and and_1 (f, A, not_1_out);
endmodule

module warmup (
  input  A,
  input  B,
  output f
);

  wire not_1_out;

  not not_1 (not_1_out, B);
  and and_1 (f, A, not_1_out);
endmodule
