// Logisim project IT012_Lab02_25521168.circ as structural Verilog
// FA1
module Warmup (
  input  [7:0] A,
  input  [7:0] B,
  output [7:0] out_3
);

  Adder adder_1 (.a(A), .b(B), .out(out_3));  // open: cin, cout
  // Probe on out_3
  // OR_Gate or_1 is placed but not wired
endmodule

module FA (
  input  A,
  input  B,
  input  Cin,
  output S,
  output Cout
);

  wire and_1_out, and_2_out, xor_1_out;

  and and_1 (and_1_out, A, B);
  and and_2 (and_2_out, Cin, xor_1_out);
  xor xor_1 (xor_1_out, A, B);
  or or_1 (Cout, and_1_out, and_2_out);
  xor xor_2 (S, xor_1_out, Cin);
endmodule

module ADDSUB4 (
  input  SUB,
  input  [3:0] B,
  input  [3:0] A,
  output [3:0] S,
  output N,
  output Z,
  output V,
  output C
);

  wire fa_1_cout, fa_2_cout, fa_3_cout, xor_1_out, xor_2_out, xor_3_out, xor_4_out, xor_5_out, xor_6_out;

  buf xor_1 (xor_1_out, B[0]);  // XOR_Gate
  buf xor_2 (xor_2_out, B[1]);  // XOR_Gate
  buf xor_3 (xor_3_out, B[2]);  // XOR_Gate
  buf xor_4 (xor_4_out, B[3]);  // XOR_Gate
  FA fa_1 (.A(xor_1_out), .B(A[0]), .Cin(SUB), .S(S[0]), .Cout(fa_1_cout));
  FA fa_2 (.A(xor_2_out), .B(A[1]), .Cin(fa_1_cout), .S(S[1]), .Cout(fa_2_cout));
  FA fa_3 (.A(xor_3_out), .B(A[2]), .Cin(fa_2_cout), .S(S[2]), .Cout(fa_3_cout));
  FA fa_4 (.A(xor_4_out), .B(A[3]), .Cin(fa_3_cout), .S(N), .Cout(C));
  nor nor_1 (Z, S[0], S[1], S[2], N);
  xor xor_5 (xor_5_out, B[3], N);
  xor xor_6 (xor_6_out, B[3], N);
  and and_1 (V, xor_5_out, xor_6_out);

  assign S[3] = N;
endmodule

module LT (
  input  A7,
  input  B7,
  input  R7,
  output LT
);

  wire and_1_out, and_2_out, and_3_out, not_1_out;

  not not_1 (not_1_out, B7);
  and and_1 (and_1_out, A7, not_1_out);
  and and_2 (and_2_out, A7, R7);
  and and_3 (and_3_out, not_1_out, R7);
  or or_1 (LT, and_1_out, and_2_out, and_3_out);
endmodule

module DLATCH (
  input  D,
  input  E,
  output Q
);

  Multiplexer #(.enable("false")) multiplexer_1 (.in0(Q), .in1(D), .out(Q), .sel(E));
endmodule

module DFF_MS (
  input  D,
  input  CLK,
  output Q
);

  wire dlatch_1_q, not_1_out;

  not not_1 (not_1_out, CLK);
  DLATCH dlatch_1 (.D(D), .E(not_1_out), .Q(dlatch_1_q));
  DLATCH dlatch_2 (.D(dlatch_1_q), .E(CLK), .Q(Q));
endmodule

module ALU8 (
  input  [7:0] A,
  input  [7:0] B,
  input  [2:0] OP,
  output [7:0] R,
  output Z,
  output LT
);

  wire [7:0] adder_1_out, adder_2_out, and_1_out, multiplexer_1_out, multiplexer_2_out, not_1_out, or_1_out,
       subtractor_1_out, subtractor_2_out, undriven, undriven_2, undriven_3, undriven_4, undriven_5,
       undriven_6, undriven_7, undriven_8, undriven_9, xor_1_p1, xor_1_p2, xor_1_p3;

  Adder #(.width(8)) adder_1 (.a(xor_1_p1), .b(xor_1_p2), .out(adder_1_out));  // open: cin, cout
  Adder #(.width(8)) adder_2 (.a(undriven), .out(adder_2_out));  // open: b, cin, cout
  Subtractor #(.width(8)) subtractor_1 (.a(undriven_2), .b(undriven_7), .out(subtractor_1_out));  // open: bin, bout
  Subtractor #(.width(8)) subtractor_2 (.a(undriven_3), .out(subtractor_2_out));  // open: b, bin, bout
  assign and_1_out = undriven_4 & undriven_8;  // AND_Gate and_1, 8 bits wide
  assign or_1_out = undriven_5 | undriven_9;  // OR_Gate or_1, 8 bits wide
  assign not_1_out = ~undriven_6;  // NOT_Gate not_1, 8 bits wide
  // XOR_Gate #(.width(8)) xor_1: pin names not known; wires that end beside it: xor_1_p1, xor_1_p2, xor_1_p3
  Multiplexer #(.select(2), .width(8), .enable("false")) multiplexer_1 (
    .in0(adder_1_out), .in1(adder_2_out), .in2(subtractor_1_out), .in3(subtractor_2_out),
    .out(multiplexer_1_out), .sel(OP[1:0]));
  Multiplexer #(.select(2), .width(8), .enable("false")) multiplexer_2 (
    .in0(and_1_out), .in1(or_1_out), .in2(not_1_out), .in3(xor_1_p3), .out(multiplexer_2_out), .sel(OP[1:0]));
  Multiplexer #(.width(8), .enable("false")) multiplexer_3 (
    .in0(multiplexer_1_out), .in1(multiplexer_2_out), .out({R[7:4], R[7:4]}), .sel(OP[2]));
  nor nor_1 (Z, R[4], R[5], R[6], R[7], R[4], R[5], R[6], R[7]);
  // LT lt_1: pin names not known; wires that end beside it: xor_1_p1[7], xor_1_p2[7], R[7], LT

  assign R[3:0] = R[7:4];
endmodule

module TN3 (
  input  D,
  input  CLK,
  output Q1,
  output Q2,
  output Q3,
  output L1,
  output L2,
  output F1,
  output F2
);

  wire d_ff_2_p2, undriven, undriven_2, undriven_3, undriven_4, undriven_5, undriven_6;

  DLATCH dlatch_1 (.D(D), .E(d_ff_2_p2), .Q(Q1));
  D_Flip_Flop d_ff_1 (.clk(undriven), .D(undriven_4), .Q(Q2));  // open: Qn, preset, en, reset
  DFF_MS dff_ms_1 (.D(undriven_2), .CLK(undriven_5), .Q(Q3));
  DLATCH dlatch_2 (.D(undriven_3), .E(undriven_6), .Q(L1));
  // D_Flip_Flop d_ff_2: pin names not known; wires that end beside it: D, d_ff_2_p2, F1
  DLATCH dlatch_3 (.D(L1), .E(undriven_6), .Q(L2));
  D_Flip_Flop d_ff_3 (.clk(F1), .D(d_ff_2_p2), .Q(F2));  // open: Qn, preset, en, reset
endmodule

module REGFILE (
  input  CLK,
  input  WE,
  input  [1:0] RD,
  input  [7:0] DIN,
  input  [1:0] RA,
  input  [1:0] RB,
  output [7:0] R0,
  output [7:0] QA,
  output [7:0] R1,
  output [7:0] R2,
  output [7:0] QB,
  output [7:0] R3
);

  wire and_1_out, and_2_out, and_3_out, and_4_out, decoder_1_out0, decoder_1_out1, decoder_1_out2,
       decoder_1_out3, undriven, undriven_2, undriven_3, undriven_7, undriven_8, undriven_9, undriven_10;
  wire [7:0] undriven_4, undriven_5, undriven_6, undriven_11, undriven_12, undriven_13, undriven_14;

  Decoder #(.select(2), .enable("false")) decoder_1 (
    .out0(decoder_1_out0), .out1(decoder_1_out1), .out2(decoder_1_out2), .out3(decoder_1_out3), .sel(RD));
  and and_1 (and_1_out, decoder_1_out0, undriven);
  and and_2 (and_2_out, decoder_1_out1, undriven_2);
  and and_3 (and_3_out, decoder_1_out2, undriven_3);
  and and_4 (and_4_out, decoder_1_out3, WE);
  Register #(.width(8)) register_1 (.D(undriven_4), .en(and_1_out), .Q(R0), .clk(undriven_7));  // open: clr
  Register #(.width(8)) register_2 (.D(undriven_5), .en(and_2_out), .Q(R1), .clk(undriven_8));  // open: clr
  Register #(.width(8)) register_3 (.D(undriven_6), .en(and_3_out), .Q(R2), .clk(undriven_9));  // open: clr
  Register #(.width(8)) register_4 (.D(undriven_4), .en(and_4_out), .Q(R3), .clk(undriven_10));  // open: clr
  Multiplexer #(.select(2), .width(8), .enable("false")) multiplexer_1 (
    .in0(undriven_11), .in1(undriven_12), .in2(undriven_13), .in3(undriven_14), .out(QA), .sel(RA));
  Multiplexer #(.select(2), .width(8), .enable("false")) multiplexer_2 (
    .in0(undriven_11), .in1(undriven_12), .in2(undriven_13), .in3(undriven_14), .out(QB), .sel(RB));
endmodule

module DATAPATH (
  input  [7:0] IMM,
  input  SRC,
  input  [2:0] OP,
  input  [1:0] RA,
  input  [1:0] RB,
  input  [1:0] RD,
  input  WE,
  input  CLK,
  output [7:0] R0,
  output [7:0] R1,
  output [7:0] R2,
  output [7:0] R3,
  output [7:0] R,
  output Z
);

  wire [7:0] multiplexer_1_out, regfile_1_qa, regfile_1_r0;

  Multiplexer #(.width(8), .enable("false")) multiplexer_1 (.in0(R), .in1(IMM), .out(multiplexer_1_out), .sel(SRC));
  REGFILE regfile_1 (
    .CLK(CLK), .WE(WE), .RD(RD), .DIN(multiplexer_1_out), .RA(RA), .RB(RB), .R0(regfile_1_r0),
    .QA(regfile_1_qa), .R1(R0), .R2(R1), .QB(R2), .R3(R3));
  ALU8 alu8_1 (.A(regfile_1_r0), .B(regfile_1_qa), .OP(OP), .R(R), .Z(Z));  // open: LT
endmodule
