// Logisim project Thi_nghiem_01.circ as structural Verilog: 1 circuit, main circuit main
module main (
  input  A,
  input  B,
  input  C,
  output A_prime,
  output \and ,
  output \or ,
  output \nand ,
  output CHAIN,
  output \nor ,
  output \xor ,
  output XOR3,
  output \xnor ,
  output NAND3
);

  not not_1 (A_prime, A);
  and and_1 (\and , A, B);
  or or_1 (\or , A, B);
  nand nand_1 (\nand , A, B);
  nor nor_1 (\nor , A, B);
  xor xor_1 (\xor , A, B);
  ExactlyOne xor_2 (.out(XOR3), .in0(A), .in1(B), .in2(C));
  xnor xnor_1 (\xnor , A, B);
  nand nand_2 (NAND3, A, B, C);
  nand nand_3 (CHAIN, \nand , C);
endmodule
