// Logisim project Thi_nghiem_04.circ as structural Verilog: 1 circuit, main circuit main
module main (
  input  A,
  input  B,
  input  C,
  input  D,
  output FPoS,
  output F_can,
  output FSoP
);

  wire A_prime_B_prime_C_out, A_prime_B_prime_CD_out, A_prime_B_prime_CD_prime_out, A_prime_BC_prime_D_out,
       A_prime_BCD_out, A_prime_CD_out, AB_prime_CD_out, ABC_prime_D_out, B_prime_CD_out, BC_prime_D_out,
       not_1_out, not_2_out, not_3_out, not_4_out, or_2_out, or_3_out, or_5_out, or_6_out;

  not not_1 (not_1_out, A);
  and A_prime_B_prime_CD_prime (A_prime_B_prime_CD_prime_out, not_1_out, not_2_out, C, not_4_out);
  not not_2 (not_2_out, B);
  and A_prime_B_prime_CD (A_prime_B_prime_CD_out, not_1_out, not_2_out, C, D);
  and A_prime_BC_prime_D (A_prime_BC_prime_D_out, A, not_2_out, not_3_out, D);
  not not_3 (not_3_out, C);
  and A_prime_BCD (A_prime_BCD_out, not_1_out, B, C, D);
  or or_1 (F_can, A_prime_B_prime_CD_prime_out, A_prime_B_prime_CD_out, A_prime_BC_prime_D_out, A_prime_BCD_out, AB_prime_CD_out, ABC_prime_D_out);
  not not_4 (not_4_out, D);
  and AB_prime_CD (AB_prime_CD_out, B, not_2_out, C, D);
  and ABC_prime_D (ABC_prime_D_out, A, B, not_3_out, D);
  or or_2 (or_2_out, B, C);
  and A_prime_B_prime_C (A_prime_B_prime_C_out, A_prime_B_prime_CD_prime_out, A_prime_B_prime_CD_out);
  and and_1 (FPoS, or_2_out, or_3_out, or_5_out, or_6_out);
  or or_3 (or_3_out, not_1_out, D);
  and BC_prime_D (BC_prime_D_out, A_prime_BC_prime_D_out, ABC_prime_D_out);
  or or_4 (FSoP, A_prime_B_prime_C_out, BC_prime_D_out, B_prime_CD_out, A_prime_CD_out);
  or or_5 (or_5_out, A, not_2_out, D);
  and B_prime_CD (B_prime_CD_out, A_prime_B_prime_CD_out, AB_prime_CD_out);
  or or_6 (or_6_out, not_1_out, not_2_out, not_3_out);
  and A_prime_CD (A_prime_CD_out, A_prime_B_prime_CD_out, A_prime_BCD_out);
endmodule
